// Logisim project logisim_simulation_complete.circ as structural Verilog: 3 circuits, main circuit main
module main (
  input  Ready,
  input  Reset,
  input  Entrada,
  input  in_4,
  input  in_5,
  input  in_6
);

  wire Codificador_s1, Codificador_s2, Codificador_s3, Codificador_s4, Codificador_s5, Display_a, Display_b,
       Display_c, Display_d, Display_e, Display_f, Display_g;

  LED S1 (.in(Codificador_s1));
  LED S2 (.in(Codificador_s2));
  LED S3 (.in(Codificador_s3));
  LED S4 (.in(Codificador_s4));
  LED S5 (.in(Codificador_s5));
  Codificador Codificador (
    .RE(Ready), .RS(Reset), .A(Entrada), .B(in_4), .C(in_5), .D(in_6), .S1(Codificador_s1),
    .S2(Codificador_s2), .S3(Codificador_s3), .S4(Codificador_s4), .S5(Codificador_s5));
  _7_Segment_Display u_7_segment_display_1 (
    .g(Display_g), .f(Display_f), .a(Display_a), .b(Display_b), .e(Display_e), .d(Display_d), .c(Display_c));  // open: dp
  Display Display (
    .S1(Codificador_s1), .S2(Codificador_s2), .S3(Codificador_s3), .S4(Codificador_s4), .S5(Codificador_s5),
    .a(Display_a), .b(Display_b), .c(Display_c), .d(Display_d), .e(Display_e), .f(Display_f), .g(Display_g));
endmodule

module Codificador (
  input  RE,
  input  RS,
  input  A,
  input  B,
  input  C,
  input  D,
  output S1,
  output S2,
  output S3,
  output S4,
  output S5
);

  wire and_1_out, and_2_out, and_3_out, and_4_out, and_5_out, and_6_out, and_7_out, and_8_out, and_9_out,
       and_10_out, and_11_out, and_12_out, and_13_out, and_14_out, and_15_out, and_16_out, and_17_out,
       and_18_out, and_19_out, and_20_out, not_1_out, not_2_out, not_3_out, not_4_out, not_5_out, not_6_out,
       not_7_out, not_8_out, not_9_out, not_10_out, not_11_out, not_12_out, not_13_out, not_14_out,
       not_15_out, not_16_out, not_17_out, not_18_out, not_19_out, not_20_out, not_21_out, not_22_out,
       not_23_out, not_24_out, not_25_out, not_26_out, not_27_out, not_28_out, not_29_out, not_30_out,
       not_31_out, not_32_out, not_33_out, not_34_out, not_35_out, not_36_out, not_37_out, not_38_out,
       not_39_out, not_40_out, not_41_out, not_42_out, not_43_out, not_44_out, not_45_out, not_46_out,
       not_47_out, not_48_out, not_49_out, not_50_out, not_51_out, not_52_out;

  not not_1 (not_1_out, RS);
  not not_2 (not_2_out, B);
  not not_3 (not_3_out, C);
  not not_4 (not_4_out, D);
  not not_5 (not_5_out, RS);
  not not_6 (not_6_out, A);
  not not_7 (not_7_out, RS);
  not not_8 (not_8_out, B);
  not not_9 (not_9_out, C);
  not not_10 (not_10_out, RS);
  not not_11 (not_11_out, B);
  not not_12 (not_12_out, D);
  not not_13 (not_13_out, RS);
  not not_14 (not_14_out, B);
  not not_15 (not_15_out, C);
  not not_16 (not_16_out, RS);
  not not_17 (not_17_out, A);
  not not_18 (not_18_out, RS);
  not not_19 (not_19_out, B);
  not not_20 (not_20_out, RS);
  not not_21 (not_21_out, B);
  not not_22 (not_22_out, C);
  not not_23 (not_23_out, RS);
  not not_24 (not_24_out, B);
  not not_25 (not_25_out, D);
  not not_26 (not_26_out, RS);
  not not_27 (not_27_out, B);
  not not_28 (not_28_out, RS);
  not not_29 (not_29_out, C);
  not not_30 (not_30_out, D);
  not not_31 (not_31_out, RS);
  not not_32 (not_32_out, A);
  not not_33 (not_33_out, B);
  not not_34 (not_34_out, RS);
  not not_35 (not_35_out, B);
  not not_36 (not_36_out, RS);
  not not_37 (not_37_out, B);
  not not_38 (not_38_out, RS);
  not not_39 (not_39_out, C);
  not not_40 (not_40_out, RS);
  not not_41 (not_41_out, A);
  not not_42 (not_42_out, B);
  not not_43 (not_43_out, RS);
  not not_44 (not_44_out, A);
  not not_45 (not_45_out, C);
  not not_46 (not_46_out, D);
  not not_47 (not_47_out, RS);
  not not_48 (not_48_out, B);
  not not_49 (not_49_out, RS);
  not not_50 (not_50_out, C);
  not not_51 (not_51_out, RS);
  not not_52 (not_52_out, D);
  and and_1 (and_1_out, RE, not_1_out, not_2_out, not_3_out, not_4_out);
  and and_2 (and_2_out, RE, not_5_out, not_6_out, B, C);
  and and_3 (and_3_out, RE, not_7_out, A, not_8_out, not_9_out);
  and and_4 (and_4_out, RE, not_10_out, A, not_11_out, not_12_out);
  and and_5 (and_5_out, RE, not_13_out, not_14_out, not_15_out);
  and and_6 (and_6_out, RE, not_16_out, not_17_out, B, C, D);
  and and_7 (and_7_out, RE, not_18_out, A, not_19_out);
  and and_8 (and_8_out, RE, not_20_out, not_21_out, not_22_out);
  and and_9 (and_9_out, RE, not_23_out, not_24_out, not_25_out);
  and and_10 (and_10_out, RE, not_26_out, A, not_27_out);
  and and_11 (and_11_out, RE, not_28_out, A, not_29_out, not_30_out);
  and and_12 (and_12_out, RE, not_31_out, not_32_out, not_33_out);
  and and_13 (and_13_out, RE, not_34_out, not_35_out, D);
  and and_14 (and_14_out, RE, not_36_out, not_37_out, C);
  and and_15 (and_15_out, RE, not_38_out, A, B, not_39_out);
  and and_16 (and_16_out, RE, not_40_out, not_41_out, not_42_out);
  and and_17 (and_17_out, RE, not_43_out, not_44_out, not_45_out, not_46_out);
  and and_18 (and_18_out, RE, not_47_out, not_48_out, C);
  and and_19 (and_19_out, RE, not_49_out, A, B, not_50_out);
  and and_20 (and_20_out, RE, not_51_out, A, B, not_52_out);
  or or_1 (S1, and_1_out, and_2_out, and_3_out, and_4_out);
  or or_2 (S2, and_5_out, and_6_out, and_7_out);
  or or_3 (S3, and_8_out, and_9_out, and_10_out, and_11_out);
  or or_4 (S4, and_12_out, and_13_out, and_14_out, and_15_out);
  or or_5 (S5, and_16_out, and_17_out, and_18_out, and_19_out, and_20_out);
endmodule

module Display (
  input  S1,
  input  S2,
  input  S3,
  input  S4,
  input  S5,
  output a,
  output b,
  output c,
  output d,
  output e,
  output f,
  output g
);

  wire and_1_out, and_2_out, and_3_out, and_4_out, and_5_out, and_6_out, and_7_out, and_8_out, and_9_out,
       and_10_out, and_11_out, not_1_out, not_2_out, not_3_out, not_4_out, not_5_out, not_6_out, not_7_out,
       not_8_out, not_9_out, not_10_out, not_11_out, not_12_out, not_13_out, not_14_out, not_15_out,
       not_16_out;

  not not_1 (not_1_out, S4);
  not not_2 (not_2_out, S2);
  not not_3 (not_3_out, S5);
  not not_4 (not_4_out, S2);
  not not_5 (not_5_out, S1);
  not not_6 (not_6_out, S3);
  not not_7 (not_7_out, S4);
  not not_8 (not_8_out, S1);
  not not_9 (not_9_out, S5);
  not not_10 (not_10_out, S3);
  not not_11 (not_11_out, S1);
  not not_12 (not_12_out, S3);
  not not_13 (not_13_out, S1);
  not not_14 (not_14_out, S3);
  not not_15 (not_15_out, S3);
  not not_16 (not_16_out, S1);
  and and_1 (and_1_out, S2, not_1_out);
  or or_1 (b, not_2_out, not_3_out);
  or or_2 (c, not_4_out, S3);
  and and_2 (and_2_out, not_5_out, not_6_out);
  and and_3 (and_3_out, S2, not_7_out);
  and and_4 (and_4_out, S2, S5);
  and and_5 (and_5_out, not_8_out, not_9_out);
  and and_6 (and_6_out, not_10_out, S4);
  and and_7 (and_7_out, not_11_out, S2);
  and and_8 (and_8_out, S2, not_12_out);
  and and_9 (and_9_out, not_13_out, not_14_out);
  and and_10 (and_10_out, S2, S4);
  and and_11 (and_11_out, not_15_out, S5);
  or or_3 (a, not_16_out, S5, and_1_out);
  or or_4 (d, and_2_out, and_3_out, and_4_out);
  or or_5 (e, and_5_out, and_6_out, and_7_out, and_8_out);
  or or_6 (f, and_9_out, and_10_out);
  or or_7 (g, and_11_out, S2);
endmodule
